# Fritzing sketch speeduino pro NA6 (saved by Fritzing 0.9.3b)
circuit board: 10cm x 10cm
breadboards: 1

parts:
  Arduino_Mega_2560 = Arduino Mega 2560 (Rev3) [part_number="Arduino Mega 2560"]
  D15 = Schottky Diode [part_number=1N5818 package="300 mil [THT]"]
  U2 = V18ZA2P [part_number=ERZV14D220 package=v18za2p]
  C18 = Ceramic Capacitor [capacitance=0.3µF package="200 mil [THT, multilayer]"]
  R41 = Resistor [tolerance=±5% resistance=750 package=THT]
  C19 = Ceramic Capacitor [capacitance=0.01µF package="200 mil [THT, multilayer]"]
  C20 = Ceramic Capacitor [capacitance=1µF package="200 mil [THT, multilayer]"]
  R48 = Resistor [tolerance=±5% resistance=100k package=THT]
  R49 = Resistor [tolerance=±5% resistance=100k power=0.25W package=THT]
  R50 = Resistor [tolerance=±5% resistance=1k package=THT]
  R51 = Resistor [tolerance=±5% resistance=1k package=THT]
  R55 = Resistor [tolerance=±5% resistance=100k package=THT]
  R56 = Resistor [tolerance=±5% resistance=100k power=0.25W package=THT]
  R57 = Resistor [tolerance=±5% resistance=1k package=THT]
  R58 = Resistor [tolerance=±5% resistance=1k package=THT]
  Q5 = Basic FET N-Channel [part_number=STP62NS04Z package="TO220 [THT]"]
  Q7 = Basic FET N-Channel [part_number=STP62NS04Z package="TO220 [THT]"]
  Q6 = Basic FET N-Channel [part_number=STP62NS04Z package="TO220 [THT]"]
  Q8 = Basic FET N-Channel [part_number=STP62NS04Z package="TO220 [THT]"]
  J6 = double row female pin header, 28 pins [form="♀ (female)"]
  J7 = double row female pin header, 28 pins [form="♀ (female)"]
  J8 = female pin header, 14 pins [form="♀ (female)"]
  Part24 = LQFP-48 [chip_label=LQFP-48 part_number=MC33814 package=LQFP]
  IC2 = SO08 [chip_label=IC part_number=TC4424AVOA package=SO]
  IC1 = SO08 [chip_label=IC part_number=TC4424AVOA package=SO]
  R35 = Resistor [tolerance=±5% resistance=100k part_number=RC0805FR-07100KL package="0805 [SMD]"]
  R37 = Resistor [tolerance=±5% resistance=100k part_number=RC0805FR-07100KL package="0805 [SMD]"]
  Part27 = SO08 [chip_label=SO08 part_number=VNLD5090-E package=SO]
  R17 = Resistor [tolerance=±5% resistance=100k package="0805 [SMD]"]
  R59 = Resistor [tolerance=±1% resistance=1k part_number=RC0805FR-071KL package="0805 [SMD]"]
  R60 = Resistor [tolerance=±1% resistance=1k part_number=RC0805FR-071KL package="0805 [SMD]"]
  R61 = Resistor [tolerance=±5% resistance=100k package="0805 [SMD]"]
  R12 = Resistor [tolerance=±5% resistance=2.4k power=0.25W package="0805 [SMD]"]
  R9 = Resistor [tolerance=±5% resistance=2.4k package="0805 [SMD]"]
  LED2 = smd LED [color="Red (633nm)" part_number="LH R974-LP-1" package="0805 [SMD]"]
  C14 = Tantalum Capacitor [capacitance=47µF voltage=10V part_number=TAJB476K006RNJ package="B 3528 [SMD, tantalum]"]
  C13 = Ceramic Capacitor [capacitance=0.1µF voltage=50V part_number=C1206C104K5RAC7867 package="1206 [SMD, multilayer]"]
  C24 = Ceramic Capacitor [capacitance=0.1µF voltage=50V part_number=C1206C104K5RAC7867 package="1206 [SMD, multilayer]"]
  C25 = Tantalum Capacitor [capacitance=47µF voltage=10V part_number=TAJB476K006RNJ package="B 3528 [SMD, tantalum]"]
  C15 = Ceramic Capacitor [capacitance=0.1µF voltage=50V part_number=C1206C104K5RAC7867 package="1206 [SMD, multilayer]"]
  R62 = Resistor [tolerance=±5% resistance=100k package="0805 [SMD]"]
  R63 = Resistor [tolerance=±5% resistance=100k package="0805 [SMD]"]
  R64 = Resistor [tolerance=±1% resistance=1k part_number=RC0805FR-071KL package="0805 [SMD]"]
  R65 = Resistor [tolerance=±1% resistance=1k part_number=RC0805FR-071KL package="0805 [SMD]"]
  Part29 = SO08 [chip_label=SO08 part_number=VNLD5090-E package=SO]
  LED4 = smd LED [color="Red (633nm)" part_number="LH R974-LP-1" package="0805 [SMD]"]
  R15 = Resistor [tolerance=±5% resistance=2.4k package="0805 [SMD]"]
  LED3 = smd LED [color="Red (633nm)" part_number="LH R974-LP-1" package="0805 [SMD]"]
  IC4 = SO16 [chip_label=SP720ABTG part_number=SP720ABTG package=SO]
  C3 = Ceramic Capacitor [capacitance=0.1µF part_number=CL21F104ZBCNNNC package="0805 [SMD, multilayer]"]
  C1 = Ceramic Capacitor [capacitance=0.1µF part_number=CL21F104ZBCNNNC package="0805 [SMD, multilayer]"]
  C7 = Ceramic Capacitor [capacitance=0.1µF part_number=CL21F104ZBCNNNC package="0805 [SMD, multilayer]"]
  C5 = Ceramic Capacitor [capacitance=0.1µF part_number=CL21F104ZBCNNNC package="0805 [SMD, multilayer]"]
  C9 = Ceramic Capacitor [capacitance=0.1µF part_number=CL21F104ZBCNNNC package="0805 [SMD, multilayer]"]
  C26 = Ceramic Capacitor [capacitance=0.1µF part_number=CL21F104ZBCNNNC package="0805 [SMD, multilayer]"]
  C27 = Ceramic Capacitor [capacitance=0.1µF part_number=CL21F104ZBCNNNC package="0805 [SMD, multilayer]"]
  R3 = Resistor [tolerance=±0.1% resistance=2.49k package="0805 [SMD]"]
  R1 = Resistor [tolerance=±0.1% resistance=2.49k package="0805 [SMD]"]
  R8 = Resistor [tolerance=±5% resistance=470 package="0805 [SMD]"]
  R18 = Resistor [tolerance=±5% resistance=2.4k package="0805 [SMD]"]
  R23 = Resistor [tolerance=±1% resistance=1k part_number=RC0805FR-071KL package="0805 [SMD]"]
  R24 = Resistor [tolerance=±1% resistance=1k part_number=RC0805FR-071KL package="0805 [SMD]"]
  R29 = Resistor [tolerance=±1% resistance=1k part_number=RC0805FR-071KL package="0805 [SMD]"]
  R30 = Resistor [tolerance=±1% resistance=1k part_number=RC0805FR-071KL package="0805 [SMD]"]
  Part30 = 174917_DENSO-ECU-socket_48pin-040-070 [part_number=174917 package="48-pin 0.40/0.70"]
  D19 = Diode [part_number=1N4448WX-TP package=sod-323]
  D18 = Diode [part_number=1N4448WX-TP package=sod-323]
  D21 = Diode [part_number=1N4448WX-TP package=sod-323]
  D20 = Diode [part_number=1N4448WX-TP package=sod-323]
  LED1 = smd LED [color="Red (633nm)" part_number="LH R974-LP-1" package="0805 [SMD]"]
  MPX4250AP1 = MPX4250AP pressure sensor [part_number=MPX]
  R4 = Resistor [tolerance=±5% resistance=470 package="0805 [SMD]"]
  R39 = Resistor [tolerance=±5% resistance=1k package="0805 [SMD]"]
  R66 = Resistor [tolerance=±5% resistance=220 package="0805 [SMD]"]
  LED8 = smd LED [color="Red (633nm)" package="0805 [SMD]"]
  LED7 = smd LED [color="Red (633nm)" part_number="LH R974-LP-1" package="0805 [SMD]"]
  LED5 = smd LED [color="Red (633nm)" part_number="LH R974-LP-1" package="0805 [SMD]"]
  LED6 = smd LED [color="Red (633nm)" part_number="LH R974-LP-1" package="0805 [SMD]"]
  R26 = Resistor [tolerance=±5% resistance=2.4k package="0805 [SMD]"]
  R36 = Resistor [tolerance=±5% resistance=100k package="0805 [SMD]"]
  R67 = Resistor [tolerance=±5% resistance=220 package="0805 [SMD]"]
  R40 = Resistor [tolerance=±5% resistance=1k package="0805 [SMD]"]
  R28 = Resistor [tolerance=±5% resistance=2.4k package="0805 [SMD]"]
  R38 = Resistor [tolerance=±5% resistance=100k package="0805 [SMD]"]
  R34 = Resistor [tolerance=±5% resistance=2.4k package="0805 [SMD]"]
  R33 = Resistor [tolerance=±5% resistance=2.4k power=0.25W package="0805 [SMD]"]
  C16 = Tantalum Capacitor [capacitance=10µF voltage=35V part_number=T491D106K050AT package="D 7343 [SMD, tantalum]"]
  U6 = DIODE-ZENER [package=diode-zener]
  R54 = Resistor [tolerance=±5% resistance=10k package="0805 [SMD]"]
  R2 = Resistor [tolerance=±5% resistance=470 package="0805 [SMD]"]
  C2 = Ceramic Capacitor [capacitance=0.22µF package="0805 [SMD, multilayer]"]
  R22 = Resistor [tolerance=±5% resistance=470 package="0805 [SMD]"]
  C10 = Ceramic Capacitor [capacitance=0.22µF package="0805 [SMD, multilayer]"]
  C23 = Ceramic Capacitor [capacitance=4.7nF package="0805 [SMD, multilayer]"]
  D23 = Diode [part_number=B0540WS-7 package=sod-323]
  C12 = Ceramic Capacitor [capacitance=1µF package="0805 [SMD, multilayer]"]
  C4 = Ceramic Capacitor [capacitance=0.22µF package="0805 [SMD, multilayer]"]
  C6 = Ceramic Capacitor [capacitance=0.22µF package="0805 [SMD, multilayer]"]
  R6 = Resistor [tolerance=±5% resistance=470 package="0805 [SMD]"]
  R7 = Resistor [tolerance=±0.1% resistance=3.9k package="0805 [SMD]"]
  R21 = Resistor [tolerance=±5% resistance=1k package="0805 [SMD]"]
  C8 = Ceramic Capacitor [capacitance=0.22µF package="0805 [SMD, multilayer]"]
  U7 = DIODE-ZENER [package=diode-zener]
  R68 = Resistor [tolerance=±5% resistance=10 part_number=RC0805FR-0710RL package="0805 [SMD]"]
  R69 = Resistor [tolerance=±5% resistance=10 part_number=RC0805FR-0710RL package="0805 [SMD]"]
  R70 = Resistor [tolerance=±5% resistance=1k package="0805 [SMD]"]
  U8 = DIODE-ZENER [part_number=MM3Z5V1ST1G package=sod-323]
  Pololu_A1 = Pololu A4988 [package=SO16]

nets:
  ADC Clamp1/IAT-CPU-A0: Arduino_Mega_2560.A0, IC4.1, R2.Pin_1, C2.1
  ADC Clamp2/CLT-CPU-A1: Arduino_Mega_2560.A1, IC4.2, R4.Pin_1, C4.1
  ADC Clamp3/TPS-CPU-A2: Arduino_Mega_2560.A2, IC4.3, C6.1, R6.Pin_1
  ADC Clamp4/CPU-A3: Arduino_Mega_2560.A3, IC4.4, R22.Pin_1, C10.1
  ADC Clamp5/BRV-CPU-A4: Arduino_Mega_2560.A4, IC4.5, R8.Pin_1, C8.1
  ADC Clamp6/CPU-A5: Arduino_Mega_2560.A5, C18.0, R41.Pin_1, IC4.6
  33814-CSB/CPU-A6: Arduino_Mega_2560.A6, Part24.10
  SCL-CPU-D21: Arduino_Mega_2560.D21/SCL
  ADC Clamp8/TACH1-CPU-D19: Arduino_Mega_2560.D19/RX1, IC4.15, C26.0, R66.Pin_1
  ADC Clamp9/TACH2-CPU-D18: Arduino_Mega_2560.D18/TX1, IC4.14, C27.1, R67.Pin_1
  STEP-CPU-D17: Arduino_Mega_2560.D17_PWM/RX2, Pololu_A1.STEP
  STEPDIR-CPU-D16: Arduino_Mega_2560.D16_PWM/TX2, Pololu_A1.DIR
  SDA-CPU-D20: Arduino_Mega_2560.SDA
  CPU-D12: Arduino_Mega_2560.D12_PWM, R70.Pin_1, U8.C
  CPU-D11: Arduino_Mega_2560.D11_PWM, R59.Pin_0, R61.Pin_0
  CPU-D10: Arduino_Mega_2560.D10_PWM, R17.Pin_0, R60.Pin_0
  CPU-D9: Arduino_Mega_2560.D9_PWM, R62.Pin_0, R64.Pin_0
  CPU-D8: Arduino_Mega_2560.D8_PWM, R63.Pin_0, R65.Pin_0
  5V/VCC: Arduino_Mega_2560.IOREF, Arduino_Mega_2560.5V, Part24.17, IC2.6, IC1.6, C14.+, C13.1, IC4.16, R39.Pin_0, R40.Pin_0, U6.C, R54.Pin_0, D23.C, C12.1, Pololu_A1.RESET, Pololu_A1.SLEEP
  RESET: Arduino_Mega_2560.RESET, R54.Pin_1, C23.1, D23.A
  GND: Arduino_Mega_2560.GND, U2.P$2, C18.1, C19.0, C20.0, R48.Pin_0, R49.Pin_0, R55.Pin_0, R56.Pin_0, Q5.source, Q7.source, Q6.source, Q8.source, Part24.15, Part24.38, Part24.40, Part24.42, IC2.3, IC1.3, R35.Pin_0, R37.Pin_0, Part27.5, Part27.7, R17.Pin_1, R61.Pin_1, C14.-, C13.0, C24.0, C25.-, C15.0, R62.Pin_1, R63.Pin_1, Part29.5, Part29.7, IC4.8, C3.0, C1.0, C7.0, C5.0, C9.0, C26.1, C27.0, MPX4250AP1.GND, LED8.cathode, LED7.cathode, LED5.cathode, LED6.cathode, R36.Pin_0, R38.Pin_0, C16.-, U6.A, C2.0, C10.0, C23.0, C12.0, C4.0, C6.0, R21.Pin_1, C8.0, U7.A, U8.A, Pololu_A1.GND
  LS2-CPU-D5: Arduino_Mega_2560.D4_PWM, R58.Pin_0
  LS3-CPU-D6: Arduino_Mega_2560.D5_PWM, R50.Pin_0
  LS4-CPU-D4: Arduino_Mega_2560.D6_PWM, R57.Pin_0
  LS1-CPU-D7: Arduino_Mega_2560.D7_PWM, R51.Pin_0
  FP-CPU-D22: Arduino_Mega_2560.D22, Part24.36
  CPU-D35: Arduino_Mega_2560.D35, R29.Pin_0
  CPU-D37: Arduino_Mega_2560.D37, R30.Pin_0
  IGN2-CPU-D24: Arduino_Mega_2560.D38
  CPU-D39: Arduino_Mega_2560.D39, R23.Pin_0
  IGN1-CPU-D28: Arduino_Mega_2560.D40
  CPU-D41: Arduino_Mega_2560.D41, R24.Pin_0
  RST-CPU-D48: Arduino_Mega_2560.D43
  LC-CPU-D45: Arduino_Mega_2560.D45
  CPU-D47: Arduino_Mega_2560.D47
  CPU-D49: Arduino_Mega_2560.D49
  MISO: Arduino_Mega_2560.D50, Part24.16
  MOSI: Arduino_Mega_2560.D51, Part24.13
  SCLK: Arduino_Mega_2560.D52, Part24.12
  CPU-D53: Arduino_Mega_2560.D53
  VRegIn: D15.cathode, Part24.11
  12V: D15.anode, U2.P$1, R12.Pin_0, R9.Pin_0, C15.1, R15.Pin_0, R18.Pin_0, Part30.1B, C16.+, R7.Pin_0, Pololu_A1.VMOT
  N1: R41.Pin_0, MPX4250AP1.V_out
  VPROT: C19.1, C20.1, J6.pin1, J6.pin28, J7.pin1, J7.pin28, J8.pin1, Part24.20, C24.1, C25.+, R3.Pin_0, R1.Pin_0, MPX4250AP1.Vs, U7.C
  N2: R48.Pin_1, R50.Pin_1, Q7.gate
  N3: R49.Pin_1, R51.Pin_1, Q8.gate
  N4: R55.Pin_1, R57.Pin_1, Q5.gate
  N5: R56.Pin_1, R58.Pin_1, Q6.gate
  HC-1-OUT: Q5.drain
  IDLE-OUT: Q7.drain, Part30.2W
  HC-2-OUT: Q6.drain
  BOOST-OUT: Q8.drain
  N6: J6.pin14, J6.pin15, J7.pin14, J7.pin15, J8.pin14
  VRSOut: Part24.7
  VRSP: Part24.8
  VRSN: Part24.9
  RESETB: Part24.19
  FP-Out: Part24.41, Part30.2O
  N7: IC2.2, R29.Pin_1, R38.Pin_1
  N8: IC2.4, R30.Pin_1, R36.Pin_1
  IGN-4-OUT: IC2.5, R34.Pin_1
  N9: IC2.7, R33.Pin_1
  N10: IC1.2, R37.Pin_1, R23.Pin_1
  N11: IC1.4, R35.Pin_1, R24.Pin_1
  N12: IC1.5, R26.Pin_1, R68.Pin_0
  N13: IC1.7, R28.Pin_1, R69.Pin_1
  N14: Part27.1, R59.Pin_1
  N15: Part27.3, R60.Pin_1
  INJ-2-OUT: Part27.6, Part30.2V, D19.C
  INJ-1-OUT: Part27.8, Part30.2U, D18.C
  N16: R12.Pin_1, LED2.anode
  N17: R9.Pin_1, LED1.anode
  N18: LED2.cathode, D19.A
  N19: R64.Pin_1, Part29.1
  N20: R65.Pin_1, Part29.3
  INJ-4-OUT: Part29.6, D21.C
  INJ-3-OUT: Part29.8, D20.C
  N21: LED4.cathode, D21.A
  N22: LED4.anode, R18.Pin_1
  N23: R15.Pin_1, LED3.anode
  N24: LED3.cathode, D20.A
  ADC Clamp7: IC4.7
  ADC Clamp14: IC4.9
  ADC Clamp13: IC4.10
  ADC Clamp12: IC4.11
  ADC Clamp11: IC4.12
  ADC Clamp10: IC4.13
  CLT Sensor: C3.1, R3.Pin_1, Part30.2Q, R4.Pin_0
  IAT Sensor: C1.1, R1.Pin_1, Part30.2P, R2.Pin_0
  N25: C7.1, R8.Pin_0, R7.Pin_1, R21.Pin_0
  TPS Sensor: C5.1, Part30.2L, R6.Pin_0
  O2 Sensor: C9.1, Part30.2N, R22.Pin_0
  IGN-1-OUT: Part30.1G, R69.Pin_0
  IGN-2-OUT: Part30.1H, R68.Pin_1
  Clutch in: Part30.1V, R70.Pin_0
  Crank: Part30.2E, R39.Pin_1, R66.Pin_0
  Cam: Part30.2G, R67.Pin_0, R40.Pin_1
  N26: D18.A, LED1.cathode
  N27: LED8.anode, R34.Pin_0
  N28: LED7.anode, R33.Pin_0
  N29: LED5.anode, R28.Pin_0
  N30: LED6.anode, R26.Pin_0
  STEP-1B-OUT: Pololu_A1.1B
  STEP-1A-OUT: Pololu_A1.1A
  STEP-2A-OUT: Pololu_A1.2A
  STEP-2B-OUT: Pololu_A1.2B

notes:
  Speeduino Pro, Inlet Air Temperature sensor
  Coolant Temperature Sensor
  Speeduino Pro, Throttle Position Sensor
  Battery Reference Voltage
  Speeduino Pro v1, Injectors
  Speeduino v0.4, Connector 1
  Speeduino v0.4, O2 Sensor
  Ignitor output 1
  Ignitor output 2
  5v
  Power supply
  IGN Out
  Crank and Cam sensors
  Speeduino Pro, MAP sensor input
  Speeduino v0.5
  Generic Outputs - High Current
  inj1
  Reset Protection - Refer AVR040 Application note
  ADC Clamping circuit
  Stepper Driver
  PWM Idle / Boost
  TAPR 1.0
  © Josh Stewart
  5V
  Arduino Mega 2560
  MC33814
  2A
  1A
  Proto Area
  Clutch input
