# Fritzing sketch Teensy 3.5 Adaptor (saved by Fritzing 0.9.3b)
breadboards: 1

parts:
  J1 = female pin header, 24 pins [form="♀ (female)"]
  J2 = female pin header, 24 pins [form="♀ (female)"]
  J3 = female pin header, 5 pins [form="♀ (female)"]  # not connected
  Part1 = Arduino Mega 2560 (Rev3)

nets:
  GND: J1.pin1, Part1.GND
  D0: J1.pin2, Part1.D0_RX0
  D1: J1.pin3, Part1.D1_TX0
  D2: J1.pin4, Part1.D3_PWM
  D3: J1.pin5, Part1.D2_PWM
  D4: J1.pin6, Part1.D4_PWM
  D5: J1.pin7, Part1.D5_PWM
  D6: J1.pin8, Part1.D6_PWM
  D7: J1.pin9, Part1.D7_PWM
  D8: J1.pin10, Part1.D8_PWM
  D9: J1.pin11, Part1.D9_PWM
  D10: J1.pin12, Part1.D10_PWM
  D11: J1.pin13, Part1.D11_PWM
  D12: J1.pin14, Part1.D12_PWM
  3.3V: J1.pin15, J2.pin22
  D24: J1.pin16
  D25: J1.pin17
  D26: J1.pin18
  D27: J1.pin19
  D28: J1.pin20
  D29: J1.pin21
  D30: J1.pin22
  D31: J1.pin23
  D32: J1.pin24
  5V: Part1.5V
