# Fritzing sketch NA Miata 48 pin (saved by Fritzing 0.9.3b)
circuit board: 4cm x 10cm
breadboards: 1

parts:
  J1 = shrouded pin header, 40 pins [form="♂ (shrouded male)"]
  R1 = Resistor [tolerance=±5% resistance=20k package=THT]
  R2 = Resistor [tolerance=±5% resistance=10k package=THT]
  D1 = Zener Diode [part_number=1N4732A breakdown_voltage=5.1V package="300 mil [THT]"]
  J2 = screw terminal, 4 pins
  J3 = screw terminal, 2 pins
  Part3 = 174917_DENSO-ECU-socket_48pin-040-070 [part_number=174917 package="48-pin 0.40/0.70"]

nets:
  INJ1: J1.pin1, J1.pin40, Part3.2U
  INJ2: J1.pin2, J1.pin39, Part3.2V
  INJ3: J1.pin3, J1.pin4, Part3.2Y
  INJ4: J1.pin5, J1.pin6, Part3.2Z
  IGN1: J1.pin7, Part3.1G
  GND: J1.pin9, J1.pin10, J1.pin12, J1.pin23, R2.Pin_0, D1.anode, J3.pin1, Part3.2A, Part3.2B, Part3.2C, Part3.2D
  Clutch-in: J1.pin14, R1.Pin_1, R2.Pin_1, D1.cathode
  Coolant: J1.pin19, Part3.2Q
  IAT: J1.pin20, J2.pin2, Part3.2P
  O2: J1.pin21, J2.pin4, Part3.2N
  TPS: J1.pin22, J2.pin3, Part3.2L
  Cam: J1.pin24, Part3.2G
  Crank: J1.pin25, Part3.2E
  5V: J1.pin28, J2.pin1
  IGN2: J1.pin34, Part3.1H
  Idle: J1.pin37, Part3.2W
  Clutch: R1.Pin_0, Part3.1V
  12V: J3.pin2, Part3.1B

notes:
  1A
  2A
  5V
  GND
  48-pin OEM ECU Connector
  12V Clutch to 5V
  12V
  IAT
  O2
  TPS
  Speeduino - NA6 Miata for v0.4
  rev C
