# Fritzing sketch schematic v0.4.1 (saved by Fritzing 0.9.2b)
circuit board: 10cm x 10cm
breadboards: 1

parts:
  Arduino_Mega_2560 = Arduino Mega 2560 (Rev3) [part_number="Arduino Mega 2560"]
  R1 = Resistor [tolerance=±0.1% resistance=2.49k part_number=RC55Y-2K49BI package=THT]
  R2 = Resistor [tolerance=±5% resistance=470 package=THT]
  R3 = Resistor [tolerance=±0.1% resistance=2.49k part_number=RC55Y-2K49BI package=THT]
  R4 = Resistor [tolerance=±5% resistance=470 package=THT]
  R6 = Resistor [tolerance=±5% resistance=470 package=THT]
  R7 = Resistor [tolerance=±0.1% resistance=3.9k package=THT]
  R8 = Resistor [tolerance=±5% resistance=470 package=THT]
  R9 = Resistor [tolerance=±5% resistance=2.4k package=THT]
  D9 = Rectifier Diode [part_number=1N4004 package="300 mil [THT]"]
  Q1 = Basic FET N-Channel [part_number=STP62NS04Z package="TO220 [THT]"]
  R10 = Resistor [tolerance=±5% resistance=1k package=THT]
  R11 = Resistor [tolerance=±5% resistance=100k package=THT]
  C7 = Ceramic Capacitor [capacitance=0.1µF package="200 mil [THT, multilayer]"]
  C1 = Ceramic Capacitor [capacitance=0.1µF package="200 mil [THT, multilayer]"]
  C3 = Ceramic Capacitor [capacitance=0.1µF package="200 mil [THT, multilayer]"]
  C5 = Ceramic Capacitor [capacitance=0.1µF package="200 mil [THT, multilayer]"]
  J3 = screw terminal, 2 pins
  R15 = Resistor [tolerance=±5% resistance=2.4k package=THT]
  D11 = Rectifier Diode [part_number=1N4004 package="300 mil [THT]"]
  Q2 = Basic FET N-Channel [part_number=STP62NS04Z package="TO220 [THT]"]
  R16 = Resistor [tolerance=±5% resistance=1k package=THT]
  R17 = Resistor [tolerance=±5% resistance=100k package=THT]
  D10 = Rectifier Diode [part_number=1N4004 package="300 mil [THT]"]
  Q3 = Basic FET N-Channel [part_number=STP62NS04Z package="TO220 [THT]"]
  R13 = Resistor [tolerance=±5% resistance=1k power=0.25W package=THT]
  R14 = Resistor [tolerance=±5% resistance=100k power=0.25W package=THT]
  R18 = Resistor [tolerance=±5% resistance=2.4k package=THT]
  D12 = Rectifier Diode [part_number=1N4004 package="300 mil [THT]"]
  Q4 = Basic FET N-Channel [part_number=VND7NV04 package="TO220 [THT]"]
  R19 = Resistor [tolerance=±5% resistance=1k package=THT]
  R20 = Resistor [tolerance=±5% resistance=100k package=THT]
  C2 = Ceramic Capacitor [capacitance=0.22µF package="200 mil [THT, multilayer]"]
  C8 = Ceramic Capacitor [capacitance=0.22µF package="200 mil [THT, multilayer]"]
  R21 = Resistor [tolerance=±5% resistance=1k package=THT]
  C9 = Ceramic Capacitor [capacitance=0.1µF package="200 mil [THT, multilayer]"]
  R22 = Resistor [tolerance=±5% resistance=470 package=THT]
  C6 = Ceramic Capacitor [capacitance=0.22µF package="200 mil [THT, multilayer]"]
  C4 = Ceramic Capacitor [capacitance=0.22µF package="200 mil [THT, multilayer]"]
  C10 = Ceramic Capacitor [capacitance=0.22µF package="200 mil [THT, multilayer]"]
  IC1 = IC, DIP package, 8 pins [chip_label=IC part_number=TC4424EPA]
  R23 = Resistor [tolerance=±5% resistance=1k package=THT]
  R24 = Resistor [tolerance=±5% resistance=1k package=THT]
  C11 = Ceramic Capacitor [capacitance=1µF package="200 mil [THT, multilayer]"]
  R25 = Resistor [tolerance=±5% resistance=160 power=2W package=THT]
  R26 = Resistor [tolerance=±5% resistance=2.4k package=THT]
  R27 = Resistor [tolerance=±5% resistance=160 power=2W package=THT]
  R28 = Resistor [tolerance=±5% resistance=2.4k package=THT]
  IC2 = IC, DIP package, 8 pins [chip_label=IC part_number=TC4424EPA]
  R29 = Resistor [tolerance=±5% resistance=1k package=THT]
  R30 = Resistor [tolerance=±5% resistance=1k package=THT]
  C12 = Ceramic Capacitor [capacitance=1µF package="200 mil [THT, multilayer]"]
  R31 = Resistor [tolerance=±5% resistance=160 power=2W package=THT]
  R33 = Resistor [tolerance=±5% resistance=2.4k power=0.25W package=THT]
  R34 = Resistor [tolerance=±5% resistance=2.4k package=THT]
  U1 = Voltage Regulator - 5V [part_number=LM2940T-5.0 package="TO220 [THT]"]
  D15 = Schottky Diode [part_number=1N5818 package="300 mil [THT]"]
  C14 = Tantalum Capacitor [capacitance=47µF voltage=10V package="200 mil [THT, tantalum]"]
  C13 = Ceramic Capacitor [capacitance=0.1µF voltage=50V package="200 mil [THT, multilayer]"]
  C15 = Ceramic Capacitor [capacitance=0.1µF voltage=50V package="200 mil [THT, multilayer]"]
  C16 = Tantalum Capacitor [capacitance=10µF voltage=35V package="200 mil [THT, tantalum]"]
  U2 = V18ZA2P [part_number=ERZV14D220 package=v18za2p]
  R35 = Resistor [tolerance=±5% resistance=100k package=THT]
  R36 = Resistor [tolerance=±5% resistance=100k package=THT]
  R37 = Resistor [tolerance=±5% resistance=100k package=THT]
  R38 = Resistor [tolerance=±5% resistance=100k package=THT]
  IC3 = IC, DIP package, 8 pins [chip_label="Dual VR Conditioner"]
  JP1 = female pin header, 3 pins [form="♀ (female)"]
  JP2 = female pin header, 3 pins [form="♀ (female)"]
  JP3 = female pin header, 3 pins [form="♀ (female)"]
  R39 = Resistor [tolerance=±5% resistance=10k package=THT]
  JP4 = female pin header, 2 pins [form="♀ (female)"]
  R40 = Resistor [tolerance=±5% resistance=10k package=THT]
  JP5 = female pin header, 2 pins [form="♀ (female)"]
  C18 = Ceramic Capacitor [capacitance=0.3µF package="200 mil [THT, multilayer]"]
  R41 = Resistor [tolerance=±5% resistance=750 package=THT]
  MPX4250A = female pin header, 6 pins [form="♀ (female)"]
  C19 = Ceramic Capacitor [capacitance=0.01µF package="200 mil [THT, multilayer]"]
  C20 = Ceramic Capacitor [capacitance=1µF package="200 mil [THT, multilayer]"]
  R48 = Resistor [tolerance=±5% resistance=100k package=THT]
  R49 = Resistor [tolerance=±5% resistance=100k power=0.25W package=THT]
  R50 = Resistor [tolerance=±5% resistance=1k package=THT]
  R51 = Resistor [tolerance=±5% resistance=1k package=THT]
  R12 = Resistor [tolerance=±5% resistance=2.4k power=0.25W package=THT]
  D16 = Zener Diode [part_number=1N5919BG breakdown_voltage=5.1V package="300 mil [THT]"]
  R54 = Resistor [tolerance=±5% resistance=10k package=THT]
  D17 = Schottky Diode [part_number=1N5818 package="300 mil [THT]"]
  R55 = Resistor [tolerance=±5% resistance=100k package=THT]
  R56 = Resistor [tolerance=±5% resistance=100k power=0.25W package=THT]
  R57 = Resistor [tolerance=±5% resistance=1k package=THT]
  R58 = Resistor [tolerance=±5% resistance=1k package=THT]
  LED5 = LED - 3mm [color="Red (633nm)" package="3 mm [THT]"]
  LED6 = LED - 3mm [color="Red (633nm)" package="3 mm [THT]"]
  LED7 = LED - 3mm [color="Red (633nm)" package="3 mm [THT]"]
  LED8 = LED - 3mm [color="Red (633nm)" package="3 mm [THT]"]
  Q5 = Basic FET N-Channel [part_number=STP62NS04Z package="TO220 [THT]"]
  R32 = Resistor [tolerance=±5% resistance=160 power=2W package=THT]
  Q7 = Basic FET N-Channel [part_number=STP62NS04Z package="TO220 [THT]"]
  Q6 = Basic FET N-Channel [part_number=STP62NS04Z package="TO220 [THT]"]
  LED4 = LED - 3mm [color="Red (633nm)" package="3 mm [THT]"]
  LED3 = LED - 3mm [color="Red (633nm)" package="3 mm [THT]"]
  LED2 = LED - 3mm [color="Red (633nm)" package="3 mm [THT]"]
  LED1 = LED - 3mm [color="Red (633nm)" package="3 mm [THT]"]
  J4 = shrouded pin header, 40 pins [form="♂ (shrouded male)"]
  Q8 = Basic FET N-Channel [part_number=STP62NS04Z package="TO220 [THT]"]
  Pololu_A1 = Pololu A4988 [part_number=DRV8825 package=SO16]
  C23 = Ceramic Capacitor [capacitance=4.7nF package="200 mil [THT, multilayer]"]
  J5 = COMPUTER-PERIPHERAL-POWER [package=computer-peripheral-power]
  U3 = IC, SIP package, 12 pins [chip_label=IC]  # not connected
  J6 = double row female pin header, 28 pins [form="♀ (female)"]
  J7 = double row female pin header, 28 pins [form="♀ (female)"]
  J8 = female pin header, 14 pins [form="♀ (female)"]
  IC4 = IC, DIP package, 8 pins [chip_label=SP721 part_number=SP721]

nets (from the pcb view):
  N1: Arduino_Mega_2560.A8, R22.Pin_1, C10.1
  N2: Arduino_Mega_2560.A15, J8.pin12
  N3: Arduino_Mega_2560.A0, R2.Pin_1, C2.1, IC4.pin7
  N4: Arduino_Mega_2560.A1, R4.Pin_1, C4.1, IC4.pin6
  N5: Arduino_Mega_2560.A2, R6.Pin_1, C6.1, IC4.pin1
  N6: Arduino_Mega_2560.A3, C18.0, R41.Pin_1, J4.pin11, IC4.pin2
  N7: Arduino_Mega_2560.A4, R8.Pin_1, C8.1, IC4.pin5
  N8: Arduino_Mega_2560.D21/SCL, Arduino_Mega_2560.SCL
  N9: Arduino_Mega_2560.D19/RX1, IC3.pin8, JP2.pin1, IC4.pin3
  N10: Arduino_Mega_2560.D18/TX1, IC3.pin7, JP3.pin3
  N11: Arduino_Mega_2560.D17_PWM/RX2, Pololu_A1.STEP
  N12: Arduino_Mega_2560.D16_PWM/TX2, Pololu_A1.DIR
  N13: Arduino_Mega_2560.D11_PWM, R19.Pin_0, R20.Pin_0
  N14: Arduino_Mega_2560.D10_PWM, R16.Pin_0, R17.Pin_0
  N15: Arduino_Mega_2560.D9_PWM, R13.Pin_0, R14.Pin_0
  N16: Arduino_Mega_2560.D8_PWM, R10.Pin_0, R11.Pin_0
  N17: Arduino_Mega_2560.RESET, R54.Pin_1, D17.anode, C23.1
  N18: Arduino_Mega_2560.5V, R1.Pin_0, R3.Pin_0, U1.output_voltage, C14.+, C13.1, IC3.pin5, JP1.pin1, R39.Pin_0, R40.Pin_0, MPX4250A.pin3, C19.1, C20.1, D16.cathode, R54.Pin_0, D17.cathode, J4.pin13, J4.pin28, Pololu_A1.RESET, Pololu_A1.SLEEP, J6.pin1, J6.pin14, J6.pin15, J6.pin28, J7.pin1, J7.pin14, J7.pin15, J7.pin28, J8.pin1, J8.pin14, IC4.pin8
  N19: Arduino_Mega_2560.D4_PWM, R58.Pin_0
  N20: Arduino_Mega_2560.D5_PWM, R50.Pin_0
  N21: Arduino_Mega_2560.D6_PWM, R57.Pin_0
  N22: Arduino_Mega_2560.D7_PWM, R51.Pin_0
  N23: Arduino_Mega_2560.D38, R24.Pin_0
  N24: Arduino_Mega_2560.D40, R23.Pin_0
  N25: Arduino_Mega_2560.D43, J8.pin7
  N26: Arduino_Mega_2560.D45, J8.pin9
  N27: Arduino_Mega_2560.D47, J8.pin8
  N28: Arduino_Mega_2560.D49, J8.pin10
  N29: Arduino_Mega_2560.D50, R30.Pin_0
  N30: Arduino_Mega_2560.D51, J8.pin11
  N31: Arduino_Mega_2560.D52, R29.Pin_0
  N32: R1.Pin_1, R2.Pin_0, C1.1, J4.pin20
  N33: R3.Pin_1, R4.Pin_0, C3.1, J4.pin19
  N34: R6.Pin_0, C5.1, J4.pin22
  N35: R7.Pin_0, R9.Pin_0, J3.pin2, R15.Pin_0, R18.Pin_0, D15.anode, C15.1, C16.+, U2.P$1, JP1.pin3, R12.Pin_0, Pololu_A1.VMOT
  N36: R7.Pin_1, R8.Pin_0, C7.1, R21.Pin_0
  N37: R9.Pin_1, LED1.anode
  N38: D9.cathode, Q1.drain, J4.pin3, J4.pin4
  N39: D9.anode, LED1.cathode
  N40: Q1.gate, R10.Pin_1
  N41: R15.Pin_1, LED3.anode
  N42: D11.cathode, Q2.drain, J4.pin5, J4.pin6
  N43: D11.anode, LED3.cathode
  N44: Q2.gate, R16.Pin_1
  N45: D10.cathode, Q3.drain, J4.pin1
  N46: D10.anode, LED2.cathode
  N47: Q3.gate, R13.Pin_1
  N48: R18.Pin_1, LED4.anode
  N49: D12.cathode, Q4.drain, R27.Pin_0, R28.Pin_1, J4.pin7
  N50: D12.anode, LED4.cathode
  N51: Q4.gate, R19.Pin_1
  N52: C9.1, R22.Pin_0, J4.pin21
  N53: IC1.pin2, R23.Pin_1, R37.Pin_1
  N54: IC1.pin4, R24.Pin_1, R35.Pin_1
  N55: IC1.pin5, R25.Pin_0
  N56: IC1.pin6, C11.1, IC2.pin6, C12.1, JP1.pin2
  N57: IC1.pin7, R27.Pin_1
  N58: R25.Pin_1, R26.Pin_1, J4.pin34
  N59: R26.Pin_0, LED6.anode
  N60: R28.Pin_0, LED5.anode
  N61: IC2.pin2, R29.Pin_1, R38.Pin_1
  N62: IC2.pin4, R30.Pin_1, R36.Pin_1
  N63: IC2.pin5, R32.Pin_0
  N64: IC2.pin7, R31.Pin_1
  N65: R31.Pin_0, R33.Pin_1, J4.pin33
  N66: R33.Pin_0, LED7.anode
  N67: R34.Pin_0, LED8.anode
  N68: R34.Pin_1, R32.Pin_1, J4.pin8
  N69: U1.input_voltage, D15.cathode
  N70: IC3.pin1, J4.pin27
  N71: IC3.pin2, JP2.pin3
  N72: IC3.pin3, JP3.pin1
  N73: IC3.pin4, J4.pin26
  N74: JP2.pin2, JP4.pin2, J4.pin25
  N75: JP3.pin2, JP5.pin1, J4.pin24
  N76: R39.Pin_1, JP4.pin1
  N77: R40.Pin_1, JP5.pin2
  N78: R41.Pin_0, MPX4250A.pin1
  N79: R48.Pin_1, R50.Pin_1, Q7.gate
  N80: R49.Pin_1, R51.Pin_1, Q8.gate
  N81: R12.Pin_1, LED2.anode
  N82: R55.Pin_1, R57.Pin_1, Q5.gate
  N83: R56.Pin_1, R58.Pin_1, Q6.gate
  N84: Q5.drain, J5.NC
  N85: Q7.drain, J5.12V
  N86: Q6.drain, J5.GND
  N87: J4.pin14, J7.pin22
  N88: J4.pin15, J7.pin21
  N89: J4.pin16, J7.pin20
  N90: J4.pin17, J7.pin19
  N91: J4.pin18, J7.pin18
  N92: J4.pin29, Pololu_A1.2B
  N93: J4.pin30, Pololu_A1.2A
  N94: J4.pin31, Pololu_A1.1A
  N95: J4.pin32, Pololu_A1.1B
  N96: Q8.drain, J5.5V

notes:
  Inlet Air Temperature sensor
  Coolant Temperature Sensor
  Speeduino v0.4, Throttle Position Sensor
  Battery Reference Voltage
  Injector 1
  Speeduino v0.4, Connector 1
  Injector 3
  Injector 2
  Injector 4
  Speeduino v0.4, O2 Sensor
  Ignitor output 1
  Ignitor output 2
  12v
  5v
  Power supply
  IGN Out
  Crank and Cam sensors
  Speeduino v0.2, MAP sensor input
  Speeduino v0.4.1
  Generic Outputs - High Current
  inj1
  VR
  Hall
  Reset Protection - Refer AVR040 Application note
  ADC Clamping circuit
  Stepper Driver
  PWM Idle / Boost
  TAPR 1.0
  © Josh Stewart
  5V
  GND
