# Fritzing sketch schematic (saved by Fritzing 0.8.3b)
circuit board: 9.70457cm x 5.63032cm
breadboards: 1

parts:
  R1 = Resistor [tolerance=±5% resistance=10k package=THT]
  U1 = Optocoupler [package=THT]
  D1 = Schottky Diode [part_number=1N5819 package="300 mil [THT]"]
  D2 = Schottky Diode [part_number=1N5819 package="300 mil [THT]"]
  R2 = Resistor [tolerance=±5% resistance=10k package=THT]
  Q1 = Basic FET N-Channel [part_number=NTD5867 package="TO220 [THT]"]
  Q2 = Basic FET N-Channel [part_number=NTD5867 package="TO220 [THT]"]
  R4 = Resistor [tolerance=±5% resistance=1k package=THT]
  R5 = Resistor [tolerance=±5% resistance=10k package=THT]
  R6 = Resistor [tolerance=±5% resistance=1k package=THT]
  Injector_Outputs = screw terminal, 2 pins
  Ignition_Outputs = screw terminal, 2 pins
  C2 = Ceramic Capacitor [capacitance=100nF package="200 mil [THT, multilayer]"]
  C1 = Ceramic Capacitor [capacitance=100nF package="200 mil [THT, multilayer]"]
  R3 = Resistor [tolerance=±5% resistance=10k package=THT]
  Inputs = screw terminal, 7 pins
  12v_Input = screw terminal, 2 pins
  Arduino_Mega_2560 = Arduino Mega 2560 (Rev3)
  JP1 = JUMPER-3-OLD [package=sj_3_paste2_3]

nets:
  N1: R1.Pin_0, R5.Pin_0, R3.Pin_1, Arduino_Mega_2560.5V
  N2: R1.Pin_1, U1.Pin_5, Arduino_Mega_2560.D2_PWM
  N3: U1.Pin_1, R2.Pin_1, Inputs.pin1
  GND: U1.Pin_2, U1.Pin_4, Q1.source, Q2.source, C2.0, C1.0, 12v_Input.pin1, Arduino_Mega_2560.GND
  N4: D1.cathode, Ignition_Outputs.pin1, C1.1
  N5: D1.anode, Arduino_Mega_2560.D7_PWM
  N6: D2.cathode, Ignition_Outputs.pin2, C2.1
  N7: D2.anode, Arduino_Mega_2560.D6_PWM
  N8: R2.Pin_0, JP1.2
  N9: Q1.gate, R4.Pin_0, R3.Pin_0
  N10: Q1.drain, Injector_Outputs.pin1
  N11: Q2.gate, R5.Pin_1, R6.Pin_1
  N12: Q2.drain, Injector_Outputs.pin2
  N13: R4.Pin_1, Arduino_Mega_2560.D9_PWM
  N14: R6.Pin_0, Arduino_Mega_2560.D8_PWM
  N15: Inputs.pin3, Arduino_Mega_2560.A0
  N16: Inputs.pin4, Arduino_Mega_2560.A1
  N17: Inputs.pin5, Arduino_Mega_2560.A2
  N18: Inputs.pin6, Arduino_Mega_2560.A3
  N19: Inputs.pin7, Arduino_Mega_2560.A4
  N20: 12v_Input.pin2, Arduino_Mega_2560.VIN, JP1.3

notes:
  5V Sensor supply
  Crank
  TPS
  MAP
  +
  -
